// Logisim project 1x8 DEMULTIPLEXER.circ as structural Verilog: 1 circuit, main circuit main
module main (
  input  A,
  input  S0,
  input  S1,
  input  S2,
  output Y0__A_S0_prime_S1_prime_S2_prime,
  output Y1__A_S0_prime_S1_prime_S2,
  output out_7,
  output out_8,
  output out_9,
  output Y5__A_S0S1_prime_S2,
  output Y6__A_S0S1S2_prime,
  output Y7__A_S0S1S2
);

  wire not_1_out, not_2_out, not_3_out;

  not not_1 (not_1_out, S0);
  not not_2 (not_2_out, S1);
  not not_3 (not_3_out, S2);
  and and_1 (Y0__A_S0_prime_S1_prime_S2_prime, A, not_1_out, not_2_out, not_3_out);
  and and_2 (Y1__A_S0_prime_S1_prime_S2, A, not_1_out, not_2_out, S2);
  and and_3 (out_7, A, not_1_out, S1, not_3_out);
  and and_4 (out_8, A, not_1_out, S1, S2);
  and and_5 (out_9, A, S0, not_2_out, not_3_out);
  and and_6 (Y5__A_S0S1_prime_S2, A, S0, not_2_out, S2);
  and and_7 (Y6__A_S0S1S2_prime, A, S0, S1, not_3_out);
  and and_8 (Y7__A_S0S1S2, A, S0, S1, S2);

  // Notes on the sheet:
  //   1 x 8 DE-MULTIPLEXER
  //   RAHUL SINHA
  //   D068
  //   Y2 (A.S0'S1S2')
  //   Y3 (A.S0'S1S2)
  //   Y4 (A.S0S1'S2')
endmodule
