// Logisim project Binary to Gray Converter.circ as structural Verilog: 1 circuit, main circuit main
module main (
  input  A,
  input  B,
  input  C,
  input  D,
  input  A_2,
  input  B_2,
  input  C_2,
  input  D_2,
  output G1,
  output B1,
  output G2,
  output B2,
  output G3,
  output B3,
  output G4,
  output B4
);

  xor xor_1 (G2, A, B);
  xor xor_2 (G3, B, C);
  xor xor_3 (G4, C, D);
  LED led_1 (.in(A));
  LED led_2 (.in(G2));
  LED led_3 (.in(G3));
  LED led_4 (.in(G4));
  xor xor_4 (B2, A_2, B_2);
  LED led_5 (.in(A_2));
  LED led_6 (.in(B2));
  xor xor_5 (B3, B2, C_2);
  LED led_7 (.in(B3));
  xor xor_6 (B4, B3, D_2);
  LED led_8 (.in(B4));

  assign B1 = A_2;
  assign G1 = A;

  // Notes on the sheet:
  //   When Binary = 1010
  //   BINARY TO GRAY CONVERTER
  //   RAHUL SINHA
  //   A⊕B
  //   B⊕C
  //   C⊕D
  //   D068
  //   When Gray = 1111
  //   GRAY TO BINARY CONVERTER
  //   A⊕B
  //   A⊕B⊕C
  //   A⊕B⊕C⊕D
  //   RAHUL SINHA
  //   D068
endmodule
