// Logisim project De multiplexer (1 X 4).circ as structural Verilog: 1 circuit, main circuit main
module main (
  input  S0,
  input  S1,
  input  A,
  output Y0,
  output Y1,
  output Y2,
  output Y3
);

  wire not_1_out, not_2_out;

  not not_1 (not_1_out, S0);
  not not_2 (not_2_out, S1);
  and and_1 (Y0, A, not_1_out, not_2_out);
  and and_2 (Y1, A, not_1_out, S1);
  and and_3 (Y2, A, S0, not_2_out);
  and and_4 (Y3, A, S0, S1);

  // Notes on the sheet:
  //   1 X 4 DE-MULTIPLEXER
  //   RAHUL SINHA
  //   D068
  //   (A.S0'S1')
  //   (A.S0'S1)
  //   (A.S0S1')
  //   (A.S0S1)
endmodule
