// Logisim project DecodersExp11.circ as structural Verilog: 1 circuit, main circuit main
module main (
  input  A0,
  input  A3,
  input  A2,
  input  A1,
  input  A0_2,
  input  A2_2,
  input  A1_2,
  input  A0_3,
  input  A1_3,
  output Y0,
  output Y1,
  output Y0_2,
  output Y0_3,
  output Y2,
  output Y1_2,
  output Y1_3,
  output Y3,
  output Y2_2,
  output Y2_3,
  output Y3_2,
  output Y3_3,
  output Y4,
  output Y4_2,
  output Y5,
  output Y5_2,
  output Y6,
  output Y6_2,
  output Y7,
  output Y7_2,
  output Y8,
  output Y9,
  output Y10,
  output Y11,
  output Y12,
  output Y13,
  output Y14,
  output Y15
);

  wire not_1_out, not_2_out, not_3_out, not_4_out, not_5_out, not_6_out, not_7_out, not_8_out, not_9_out;

  not not_1 (not_1_out, A0);
  not not_2 (not_2_out, A1_3);
  and and_1 (Y0, not_1_out, not_2_out);
  and and_2 (Y1, not_1_out, A1_3);
  and and_3 (Y2, A0, not_2_out);
  and and_4 (Y3, A0, A1_3);
  not not_3 (not_3_out, A2_2);
  not not_4 (not_4_out, A0_3);
  not not_5 (not_5_out, A1_2);
  and and_5 (Y0_3, not_4_out, not_5_out, not_3_out);
  and and_6 (Y1_3, A0_3, not_5_out, not_3_out);
  and and_7 (Y2_3, not_4_out, A1_2, not_3_out);
  and and_8 (Y3_3, A0_3, A1_2, not_3_out);
  and and_9 (Y4_2, not_4_out, not_5_out, A2_2);
  and and_10 (Y5_2, A0_3, not_5_out, A2_2);
  and and_11 (Y6_2, not_4_out, A1_2, A2_2);
  and and_12 (Y7_2, A0_3, A1_2, A2_2);
  not not_6 (not_6_out, A3);
  not not_7 (not_7_out, A2);
  not not_8 (not_8_out, A1);
  not not_9 (not_9_out, A0_2);
  and and_13 (Y0_2, not_9_out, not_8_out, not_7_out, not_6_out);
  and and_14 (Y1_2, A0_2, not_8_out, not_7_out, not_6_out);
  and and_15 (Y2_2, not_9_out, A1, not_7_out, not_6_out);
  and and_16 (Y3_2, A0_2, A1, not_7_out, not_6_out);
  and and_17 (Y4, not_9_out, not_8_out, A2, not_6_out);
  and and_18 (Y5, A0_2, not_8_out, A2, not_6_out);
  and and_19 (Y6, not_9_out, A1, A2, not_6_out);
  and and_20 (Y7, A0_2, A1, A2, not_6_out);
  and and_21 (Y8, not_9_out, not_8_out, not_7_out, A3);
  and and_22 (Y9, A0_2, not_8_out, not_7_out);
  and and_23 (Y10, not_9_out, A1, not_7_out, A3);
  and and_24 (Y11, A0_2, A1, not_7_out, A3);
  and and_25 (Y12, not_9_out, not_8_out, A2, A3);
  and and_26 (Y13, A0_2, not_8_out, A2, A3);
  and and_27 (Y14, not_9_out, A1, A2, A3);
  and and_28 (Y15, A0_2, A1, A2, A3);

  // Notes on the sheet:
  //   2 to 4 Decoder
  //   3 to 8 Decoder
  //   4 to 16 Decoder
  //   Rahul Sinha
  //   D068
endmodule
