// Logisim project Encoders.circ as structural Verilog: 1 circuit, main circuit main
module main (
  input  Y3,
  input  Y2,
  input  Y1,
  input  Y9,
  input  Y8,
  input  Y7,
  input  Y6,
  input  Y5,
  input  Y4,
  input  Y3_2,
  input  Y2_2,
  input  Y1_2,
  input  Y7_2,
  input  Y6_2,
  input  Y5_2,
  input  Y4_2,
  input  Y3_3,
  input  Y2_3,
  input  Y1_3,
  output A0,
  output A1,
  output A0_2,
  output A1_2,
  output A0_3,
  output A2,
  output A1_3,
  output A3,
  output A2_2
);

  or or_1 (A0, Y1, Y3);
  or or_2 (A1, Y2, Y3);
  or or_3 (A0_3, Y1_3, Y3_3, Y5_2, Y7_2);
  or or_4 (A1_3, Y2_3, Y3_3, Y6_2, Y7_2);
  or or_5 (A2_2, Y4_2, Y5_2, Y6_2, Y7_2);
  or or_6 (A0_2, Y1_2, Y3_2, Y5, Y7, Y9);
  or or_7 (A1_2, Y2_2, Y3_2, Y6, Y7);
  or or_8 (A2, Y4, Y5, Y6, Y7);
  or or_9 (A3, Y8, Y9);

  // Notes on the sheet:
  //   8:3 Encoder
  //   4:2 Encoder
  //   Rahul Sinha
  //   D068
  //   Rahul Sinha
  //   D068
  //   Octal To Binary (10:4)  Encoder
  //   Rahul Sinha
  //   D068
endmodule
