// Logisim project FlipFlops.circ as structural Verilog: 1 circuit, main circuit main
module main (
  input  D,
  input  J,
  input  K,
  input  S_prime,
  input  R,
  input  R_prime,
  input  S,
  output Q,
  output Q_2,
  output Q_prime,
  output Q_prime_2,
  output Q_3,
  output Q_4,
  output Q_prime_3,
  output Q_prime_4
);

  wire clock_1_out, clock_2_out, nand_1_out, nand_2_out, nand_7_out, nand_8_out, not_1_out;

  Clock clock_1 (.out(clock_1_out));
  not not_1 (not_1_out, D);
  nand nand_1 (nand_1_out, D, clock_1_out);
  nand nand_2 (nand_2_out, clock_1_out, not_1_out);
  nand nand_3 (Q_2, nand_1_out, Q_prime_2);
  nand nand_4 (Q_prime_2, Q_2, nand_2_out);
  nand nand_5 (Q_3, S_prime, Q_prime_3);
  nand nand_6 (Q_prime_3, Q_3, R_prime);
  Clock clock_2 (.out(clock_2_out));
  nor nor_1 (Q_4, R, Q_prime_4);
  nor nor_2 (Q_prime_4, Q_4, S);
  nand nand_7 (nand_7_out, Q_prime, J, clock_2_out);
  nand nand_8 (nand_8_out, clock_2_out, K, Q);
  nand nand_9 (Q, nand_7_out, Q_prime);
  nand nand_10 (Q_prime, Q, nand_8_out);

  // Notes on the sheet:
  //   CLK
  //   D Flip-Flop
  //   Basic Flip-Flop (using NAND)
  //   S'
  //   R'
  //   Rahul Sinha
  //   D068
  //   Rahul Sinha
  //   D068
  //   JK Flip-Flop
  //   CLK
  //   Basic Flip-Flop (using NOR)
  //   Rahul Sinha
  //   D068
  //   Rahul Sinha
  //   D068
endmodule
