// Logisim project Full Subtractor.circ as structural Verilog: 1 circuit, main circuit main
module main (
  input  A,
  input  B,
  input  C,
  input  A_2,
  input  B_2,
  input  C_2,
  output out_7,
  output out_8,
  output out_9
);

  wire and_1_out, and_2_out, and_3_out, and_4_out, and_5_out, and_6_out, not_1_out, not_2_out, not_3_out,
       not_4_out, not_5_out, not_6_out, not_7_out, or_1_out, or_2_out, xor_1_out;

  xor xor_1 (xor_1_out, A, B);
  not not_1 (not_1_out, A_2);
  not not_2 (not_2_out, B_2);
  not not_3 (not_3_out, A_2);
  not not_4 (not_4_out, C_2);
  not not_5 (not_5_out, A_2);
  not not_6 (not_6_out, xor_1_out);
  not not_7 (not_7_out, A);
  and and_1 (and_1_out, not_1_out, not_2_out, C_2);
  and and_2 (and_2_out, not_3_out, B_2, not_4_out);
  and and_3 (and_3_out, not_5_out, B_2, C_2);
  and and_4 (and_4_out, A_2, B_2, C_2);
  xor xor_2 (out_7, xor_1_out, C);
  LED led_1 (.in(out_7));
  or or_1 (or_1_out, and_1_out, and_2_out);
  and and_5 (and_5_out, not_6_out, C);
  and and_6 (and_6_out, not_7_out, B);
  or or_2 (or_2_out, or_1_out, and_3_out);
  or or_3 (out_9, or_2_out, and_4_out);
  or or_4 (out_8, and_5_out, and_6_out);
  LED led_2 (.in(out_8));
  LED led_3 (.in(out_9));

  // Notes on the sheet:
  //   A⊕B
  //   FULL SUBTRACTOR
  //   A⊕B⊕C
  //   (A⊕B)'C
  //   A'B
  //   DIFFERENCE
  //   Rahul Sinha 
  //   D068
  //   (A⊕B)'.C + A'B
  //   BORROW
endmodule
