// Logisim project Half Adder.circ as structural Verilog: 1 circuit, main circuit main
module main (
  input  A,
  input  A_2,
  input  B,
  input  B_2,
  input  A_3,
  input  A_4,
  input  B_3,
  input  B_4,
  input  A_5,
  input  A_6,
  input  B_5,
  input  B_6,
  input  A_7,
  input  A_8,
  input  B_7,
  input  B_8,
  output S,
  output S_2,
  output C,
  output C_2,
  output S_3,
  output S_4,
  output C_3,
  output C_4,
  output S_5,
  output S_6,
  output C_5,
  output C_6,
  output S_7,
  output S_8,
  output C_7,
  output C_8
);

  wire and_2_out, and_3_out, and_6_out, and_7_out, and_10_out, and_11_out, and_14_out, and_15_out, not_1_out,
       not_2_out, not_3_out, not_4_out, not_5_out, not_6_out, not_7_out, not_8_out;

  not not_1 (not_1_out, A_3);
  not not_2 (not_2_out, B_3);
  not not_3 (not_3_out, A_7);
  not not_4 (not_4_out, B_7);
  xor xor_1 (S, A, B);
  and and_1 (C, A, B);
  and and_2 (and_2_out, not_1_out, B_3);
  and and_3 (and_3_out, not_2_out, A_3);
  and and_4 (C_3, A_3, B_3);
  xor xor_2 (S_5, A_5, B_5);
  and and_5 (C_5, A_5, B_5);
  and and_6 (and_6_out, not_3_out, B_7);
  and and_7 (and_7_out, not_4_out, A_7);
  and and_8 (C_7, A_7, B_7);
  or or_1 (S_3, and_2_out, and_3_out);
  or or_2 (S_7, and_6_out, and_7_out);
  not not_5 (not_5_out, A_4);
  not not_6 (not_6_out, B_4);
  not not_7 (not_7_out, A_8);
  not not_8 (not_8_out, B_8);
  xor xor_3 (S_2, A_2, B_2);
  and and_9 (C_2, A_2, B_2);
  and and_10 (and_10_out, not_5_out, B_4);
  and and_11 (and_11_out, not_6_out, A_4);
  and and_12 (C_4, A_4, B_4);
  xor xor_4 (S_6, A_6, B_6);
  and and_13 (C_6, A_6, B_6);
  and and_14 (and_14_out, not_7_out, B_8);
  and and_15 (and_15_out, not_8_out, A_8);
  and and_16 (C_8, A_8, B_8);
  or or_3 (S_4, and_10_out, and_11_out);
  or or_4 (S_8, and_14_out, and_15_out);

  // Notes on the sheet:
  //   A'
  //   B'
  //   A'
  //   B'
  //   A'
  //   B'
  //   A'
  //   B'
  //   Rahul Sinha
  //   70022300517
  //   HALF ADDER WITH SPECIAL AND BASIC GATES
endmodule
