// Logisim project Half Subtractor_R.circ as structural Verilog: 1 circuit, main circuit main
module main (
  input  A,
  input  B,
  input  A_2,
  input  B_2,
  output A_prime_B_AB_prime,
  output A_prime_B,
  output A_prime_B_AB_prime_2,
  output out_8
);

  wire and_2_out, and_3_out, not_1_out, not_2_out, not_3_out, not_4_out;

  not not_1 (not_1_out, A_2);
  not not_2 (not_2_out, A_2);
  xor xor_1 (A_prime_B_AB_prime, A, B);
  not not_3 (not_3_out, A);
  not not_4 (not_4_out, B_2);
  LED led_1 (.in(A_prime_B_AB_prime));
  and and_1 (A_prime_B, not_3_out, B);
  LED led_2 (.in(A_prime_B));
  and and_2 (and_2_out, not_1_out, B_2);
  and and_3 (and_3_out, not_4_out, A_2);
  and and_4 (out_8, not_2_out, B_2);
  or or_1 (A_prime_B_AB_prime_2, and_2_out, and_3_out);
  LED led_3 (.in(A_prime_B_AB_prime_2));
  LED led_4 (.in(out_8));

  // Notes on the sheet:
  //   When A=1 B=1,
  //   When A=1 B=1,
  //   HALF SUBTRACTOR ( BASIC GATES & SPECIAL GATES )
  //   DIFFERENCE
  //   A'B
  //   AB'
  //   BORROW
  //   A'B
  //   Rahul Sinha 
  //   D068
  //   DIFFERENCE
  //   BORROW
endmodule
