// Logisim project Multiplexer DIRECT.circ as structural Verilog: 1 circuit, main circuit main
module main (
  input  in_1,
  input  in_2,
  input  in_3,
  input  in_4,
  input  in_5,
  input  in_6,
  input  in_7,
  input  [2:0] in_8,
  input  in_9
);

  wire multiplexer_1_out;

  Multiplexer #(.select(3), .enable("false")) multiplexer_1 (
    .in0(in_1), .in1(in_2), .in2(in_3), .in3(in_4), .in4(in_5), .in5(in_6), .in6(in_7), .in7(in_9),
    .out(multiplexer_1_out), .sel(in_8));
  LED led_1 (.in(multiplexer_1_out));

  // Notes on the sheet:
  //   Multiplexers
  //   Rahul Sinha
  //   D068
endmodule
