// Logisim project Multiplexers.circ as structural Verilog: 1 circuit, main circuit main
module main (
  input  A0,
  input  A0_2,
  input  A1,
  input  A1_2,
  input  A2,
  input  A2_2,
  input  A3,
  input  A3_2,
  input  A4,
  input  S0,
  input  S1,
  input  A5,
  input  A6,
  input  A7,
  input  S0_2,
  input  S1_2,
  input  S2,
  output Y,
  output Y_2
);

  wire and_1_out, and_2_out, and_3_out, and_4_out, and_5_out, and_6_out, and_7_out, and_8_out, and_9_out,
       and_10_out, and_11_out, and_12_out, not_1_out, not_2_out, not_3_out, not_4_out, not_5_out, not_6_out,
       not_7_out;

  not not_1 (not_1_out, S0);
  not not_2 (not_2_out, S1);
  not not_3 (not_3_out, S0);
  not not_4 (not_4_out, S1);
  and and_1 (and_1_out, A0_2, not_1_out, not_2_out);
  and and_2 (and_2_out, A1_2, not_3_out, S1);
  and and_3 (and_3_out, A2_2, S0, not_4_out);
  and and_4 (and_4_out, A3_2, S0, S1);
  or or_1 (Y, and_1_out, and_2_out, and_3_out, and_4_out);
  LED led_1 (.in(Y));
  not not_5 (not_5_out, S0_2);
  not not_6 (not_6_out, S1_2);
  not not_7 (not_7_out, S2);
  and and_5 (and_5_out, A0, not_5_out, not_6_out, not_7_out);
  and and_6 (and_6_out, A1, not_5_out, not_6_out, S2);
  and and_7 (and_7_out, A2, not_5_out, S1_2, not_7_out);
  and and_8 (and_8_out, A3, S1_2, not_5_out, not_7_out);
  and and_9 (and_9_out, A4, S0_2, not_6_out, not_7_out);
  and and_10 (and_10_out, A5, S0_2, not_6_out, S2);
  and and_11 (and_11_out, A6, S0_2, S1_2, not_7_out);
  and and_12 (and_12_out, A7, S0_2, S1_2, S2);
  or or_2 (Y_2, and_5_out, and_6_out, and_7_out, and_8_out, and_9_out, and_10_out, and_11_out, and_12_out);
  LED led_2 (.in(Y_2));

  // Notes on the sheet:
  //   4x1 MULTIPLEXER
  //   Rahul Sinha
  //   D068
  //   S0'
  //   S1'
  //   S2'
  //   8x1 MULTIPLEXER
  //   Rahul Sinha
  //   D068
endmodule
