// Logisim project SR Flip Flop.circ as structural Verilog: 1 circuit, main circuit main
module main (
  input  R,
  input  S,
  input  S_2,
  input  R_2,
  output Q,
  output Q_2,
  output Q_prime,
  output Q_prime_2
);

  wire and_1_out, and_2_out, clock_1_out, clock_2_out, nand_1_out, nand_2_out, or_1_out, or_2_out;

  Clock clock_1 (.out(clock_1_out));
  nand nand_1 (nand_1_out, S, clock_1_out);
  nand nand_2 (nand_2_out, clock_1_out, R_2);
  nand nand_3 (Q_2, nand_1_out, Q_prime_2);
  nand nand_4 (Q_prime_2, Q_2, nand_2_out);
  Clock clock_2 (.out(clock_2_out));
  and and_1 (and_1_out, R, clock_2_out);
  and and_2 (and_2_out, clock_2_out, S_2);
  or or_1 (or_1_out, and_1_out, Q_prime);
  or or_2 (or_2_out, Q, and_2_out);
  not not_1 (Q, or_1_out);
  not not_2 (Q_prime, or_2_out);

  // Notes on the sheet:
  //   Using NAND Gate
  //   CLK
  //   Rahul Sinha
  //   D068
  //   SR Flip Flop
  //   CLK
  //   Using Basic Gates
  //   Rahul Sinha
  //   D068
endmodule
