// Logisim project demorgan 1st law.circ as structural Verilog: 1 circuit, main circuit main
module main (
  input  A,
  input  A_2,
  input  B,
  input  B_2,
  input  A_3,
  input  A_4,
  input  B_3,
  input  B_4,
  input  A_5,
  input  A_6,
  input  B_5,
  input  B_6,
  input  A_7,
  input  A_8,
  input  B_7,
  input  B_8,
  output Z,
  output Z_2,
  output A_prime__B_prime,
  output Z_3,
  output Z_4,
  output Z_5,
  output Z_6,
  output A_prime__B_prime_2
);

  wire not_1_out, not_2_out, not_3_out, not_4_out, not_7_out, not_8_out, not_9_out, not_10_out, or_1_out,
       or_2_out, or_3_out, or_4_out;

  or or_1 (or_1_out, A, B);
  not not_1 (not_1_out, A_3);
  not not_2 (not_2_out, B_3);
  or or_2 (or_2_out, A_5, B_5);
  not not_3 (not_3_out, A_7);
  not not_4 (not_4_out, B_7);
  not not_5 (Z, or_1_out);
  and and_1 (A_prime__B_prime, not_1_out, not_2_out);
  not not_6 (Z_4, or_2_out);
  and and_2 (Z_6, not_3_out, not_4_out);
  LED led_1 (.in(Z));
  LED led_2 (.in(A_prime__B_prime));
  LED led_3 (.in(Z_4));
  LED led_4 (.in(Z_6));
  or or_3 (or_3_out, A_2, B_2);
  not not_7 (not_7_out, A_4);
  not not_8 (not_8_out, B_4);
  or or_4 (or_4_out, A_6, B_6);
  not not_9 (not_9_out, A_8);
  not not_10 (not_10_out, B_8);
  not not_11 (Z_2, or_3_out);
  and and_3 (Z_3, not_7_out, not_8_out);
  not not_12 (Z_5, or_4_out);
  and and_4 (A_prime__B_prime_2, not_9_out, not_10_out);
  LED led_5 (.in(Z_2));
  LED led_6 (.in(Z_3));
  LED led_7 (.in(Z_5));
  LED led_8 (.in(A_prime__B_prime_2));

  // Notes on the sheet:
  //   INPUT: A=0 & B=0
  //   INPUT: A=1 & B=0
  //   (A + B)'
  //   (A + B)'
  //   A'. B'
  //   RAHUL SINHA
  //   D068
  //   Z
  //   RAHUL SINHA
  //   D068
  //   De Morgan's 1st Law
  //   (A + B)' = A'. B'
  //   INPUT: A=0 & B=1
  //   INPUT: A=1 & B=1
  //   RAHUL SINHA
  //   (A + B)'
  //   A'. B'
  //   RAHUL SINHA
  //   (A + B)'
  //   D068
  //   D068
  //   Z
endmodule
