// Logisim project demorgan 2nd law.circ as structural Verilog: 1 circuit, main circuit main
module main (
  input  A,
  input  A_2,
  input  B,
  input  B_2,
  input  A_3,
  input  A_4,
  input  B_3,
  input  B_4,
  input  A_5,
  input  A_6,
  input  B_5,
  input  B_6,
  input  A_7,
  input  A_8,
  input  B_7,
  input  B_8,
  input  A_9,
  input  B_9,
  output Z,
  output Z_2,
  output Z_3,
  output Z_4,
  output Z_5,
  output Z_6,
  output Z_7,
  output Z_8,
  output Z_9
);

  wire and_1_out, and_2_out, and_3_out, and_4_out, and_5_out, not_1_out, not_2_out, not_3_out, not_4_out,
       not_8_out, not_9_out, not_10_out, not_11_out;

  not not_1 (not_1_out, A_3);
  not not_2 (not_2_out, B_3);
  not not_3 (not_3_out, A_7);
  not not_4 (not_4_out, B_7);
  and and_1 (and_1_out, A, B);
  not not_5 (Z, and_1_out);
  or or_1 (Z_3, not_1_out, not_2_out);
  and and_2 (and_2_out, A_5, B_5);
  or or_2 (Z_7, not_3_out, not_4_out);
  and and_3 (and_3_out, A_9, B_9);
  LED led_1 (.in(Z));
  LED led_2 (.in(Z_3));
  not not_6 (Z_5, and_2_out);
  LED led_3 (.in(Z_5));
  LED led_4 (.in(Z_7));
  not not_7 (Z_9, and_3_out);
  LED led_5 (.in(Z_9));
  and and_4 (and_4_out, A_2, B_2);
  not not_8 (not_8_out, A_4);
  not not_9 (not_9_out, B_4);
  and and_5 (and_5_out, A_6, B_6);
  not not_10 (not_10_out, A_8);
  not not_11 (not_11_out, B_8);
  not not_12 (Z_2, and_4_out);
  LED led_6 (.in(Z_2));
  or or_3 (Z_4, not_8_out, not_9_out);
  LED led_7 (.in(Z_4));
  not not_13 (Z_6, and_5_out);
  or or_4 (Z_8, not_10_out, not_11_out);
  LED led_8 (.in(Z_8));
  LED led_9 (.in(Z_6));

  // Notes on the sheet:
  //   INPUT: A=0 & B=0
  //   INPUT: A=1 & B=0
  //   INPUT: A=1 & B=1
  //   (A .  B)'
  //   A' + B'
  //   (A . B)'
  //   A' +  B'
  //   (A .  B)'
  //   RAHUL SINHA
  //   D068
  //   RAHUL SINHA
  //   D068
  //   De Morgan's 2nd Law
  //    (A . B)' = A' + B'
  //   INPUT: A=0 & B=1
  //   INPUT: A=1 & B=1
  //   D068
  //   RAHUL SINHA
  //   (A .  B)'
  //   A' + B'
  //   RAHUL SINHA
  //   (A .  B)'
  //   A' + B'
  //   RAHUL SINHA
  //   D068
  //   D068
endmodule
